# Fritzing sketch 555 Timer IC (saved by Fritzing 0.9.2b)
circuit board: 7.09567cm x 2.08374cm
breadboards: 1

parts:
  U1 = 555 Timer [package="DIP8 [THT]"]
  VCC1 = Battery
  R1 = Resistor [tolerance=±5% resistance=4.7k package=THT]
  LED1 = LED - 5mm [color="Red (633nm)" package="5 mm [THT]"]
  C2 = Ceramic Capacitor [capacitance=0.1nF package="100 mil [THT, multilayer]"]
  C1 = Electrolytic Capacitor [capacitance=1µF package="100 mil [THT, electrolytic]"]
  R4 = Resistor [tolerance=±5% resistance=330 package=THT]
  part = Resistor [tolerance=±5% resistance=220 package=THT]  # not connected
  R3 = Rotary Potentiometer (Large) [maximum_resistance=100kΩ package=THT]

nets:
  N1: U1.Ground, VCC1.-, LED1.cathode, C2.0, C1.-
  N2: U1.Trigger, C1.+
  N3: U1.Output, R4.Pin_1
  N4: U1.Reset, U1.Vcc_Supply_Voltage, VCC1.+, R1.Pin_1
  N5: U1.Control_Voltage, C2.1
  N6: U1.Threshold, R1.Pin_0, R3.wiper
  N7: U1.Discharge, R3.leg2
  N8: LED1.anode, R4.Pin_0

notes:
  ATS ioLab 555
